# Fritzing sketch project 2 (saved by Fritzing 0.9.6b)
breadboards: 1

parts:
  Argon1 = Particle Argon
  S1 = Pushbutton [package="[SMD]"]
  S2 = Pushbutton [package="[SMD]"]
  S3 = Pushbutton [package="[SMD]"]
  LCM1602_IIC3 = LCM1602 IIC [part_number="LCM1602 IIC" chip_label="LCM1602 IIC" package="DIP (Dual Inline) [THT]"]
  U1 = LCD-16X2 [package=lcd-16x2]
  R1 = Resistor [tolerance=±5% power=0.25 resistance=220 package=THT]
  R2 = Resistor [tolerance=±5% power=0.25 resistance=220 package=THT]
  R3 = Resistor [tolerance=±5% power=0.25 resistance=220 package=THT]

nets:
  3.3V: Argon1.3.3V, LCM1602_IIC3.VCC
  GND: Argon1.GND, LCM1602_IIC3.GND, R1.Pin_1, R2.Pin_1, R3.Pin_1
  N1: Argon1.SDA, LCM1602_IIC3.SDA
  N2: Argon1.SCL, LCM1602_IIC3.SCL
  N3: Argon1.D3, S1.Pin_1, S1.Pin_2
  N4: Argon1.D4, S2.Pin_1, S2.Pin_2
  N5: Argon1.D5, S3.Pin_1, S3.Pin_2
  N6: S1.Pin_3, S1.Pin_4, R1.Pin_0
  N7: S2.Pin_3, S2.Pin_4, R2.Pin_0
  N8: S3.Pin_3, S3.Pin_4, R3.Pin_0
  VSS: LCM1602_IIC3.VSS, U1.VSS
  VDD: LCM1602_IIC3.VDD, U1.VDD
  N9: LCM1602_IIC3.V0, U1.VO
  N10: LCM1602_IIC3.RS, U1.RS
  N11: LCM1602_IIC3.RW, U1.R_W
  N12: LCM1602_IIC3.E, U1.E
  N13: LCM1602_IIC3.D0, U1.DB0
  N14: LCM1602_IIC3.D1, U1.DB1
  N15: LCM1602_IIC3.D2, U1.DB2
  N16: LCM1602_IIC3.D3, U1.DB3
  N17: LCM1602_IIC3.D4, U1.DB4
  N18: LCM1602_IIC3.D5, U1.DB5
  N19: LCM1602_IIC3.D6, U1.DB6
  N20: LCM1602_IIC3.D7, U1.DB7
  N21: LCM1602_IIC3.A, U1.A
  N22: LCM1602_IIC3.K, U1.K

custom parts:
  Particle Argon: The Argon is a powerful Wi-Fi enabled development board that can act as either a standalone Wi-Fi endpoint or Wi-Fi enabled gateway for Particle Mesh networks. It is based on the Nordic nRF52840 and has built-in battery charging circuitry so it’s easy to connect a Li-Po and deploy your local network in minutes. The Argon is great for connecting existing projects to the Particle Device Cloud or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
  LCM1602 IIC: I2C-Module to use a 1602 or 2004 LCD on with the wire.h libory Serial LCD Modul
